# Fritzing sketch christmas-tree (saved by Fritzing 0.9.3b)
breadboards: 1

parts:
  Micro_bit1 = Microbit
  LED1 = smd LED [color="Green (565nm)" package="0805 [SMD]"]
  LED2 = smd LED [color="Red (633nm)" package="0805 [SMD]"]
  LED3 = smd LED [color="Yellow (585nm)" package="0805 [SMD]"]
  LED4 = smd LED [color="Yellow (585nm)" package="0805 [SMD]"]
  LED5 = smd LED [color="Blue (470nm)" package="0805 [SMD]"]
  LED6 = smd LED [color="Green (555nm)" package="0805 [SMD]"]
  LED7 = smd LED [color="Yellow (585nm)" package="0805 [SMD]"]
  LED8 = smd LED [color="Red (633nm)" package="0805 [SMD]"]
  LED9 = smd LED [color="Green (565nm)" package="0805 [SMD]"]
  LED10 = smd LED [color="Blue (470nm)" package="0805 [SMD]"]
  LED11 = smd LED [color="Green (555nm)" package="0805 [SMD]"]
  LED12 = smd LED [color="Yellow (585nm)" package="0805 [SMD]"]

nets:
  N1: Micro_bit1.GND, LED1.cathode, LED5.cathode, LED8.cathode, LED10.cathode, LED11.cathode, LED12.cathode
  N2: Micro_bit1.0, LED1.anode
  N3: Micro_bit1.1, LED2.anode
  N4: Micro_bit1.9, LED11.anode
  N5: Micro_bit1.10, LED10.anode
  N6: Micro_bit1.2, LED3.anode
  N7: Micro_bit1.4, LED4.anode
  N8: Micro_bit1.8, LED8.anode
  N9: Micro_bit1.7, LED7.anode
  N10: Micro_bit1.6, LED9.anode
  N11: Micro_bit1.5, LED6.anode
  N12: Micro_bit1.11, LED12.anode
  N13: Micro_bit1.3, LED5.anode

custom parts:
  Microbit: BBC Microbit Fritzing part
